# Fritzing sketch Schematic (saved by Fritzing 0.9.3b)
breadboards: 1

parts:
  SDD1306 = Grove OLED 128x96
  S1 = SWITCH-MOMENTARY-2 [package=tactile-pth]
  R1 = TRIMPOT [package=trimpot-5mm]
  Teensy_3_2 = Teensy 3.1
  V1 = DC Power [voltage=5V]

nets:
  GND: SDD1306.GND, S1.2, R1.CCW, Teensy_3_2.GND, V1.V-
  VCC: SDD1306.VCC, R1.CW, Teensy_3_2.3V3
  N1: SDD1306.SDA, Teensy_3_2.A14/DAC
  N2: SDD1306.SCL, Teensy_3_2.Program
  N3: S1.1, Teensy_3_2.D6
  N4: R1.WIPER, Teensy_3_2.D12
  N5: Teensy_3_2.Vin, V1.V+
